// Logisim project version1.circ as structural Verilog: 1 circuit, main circuit main
module main (
  input  A,
  input  B,
  input  E,
  output Valid,
  output Direction
);


  // Notes on the sheet:
  //   Enable:  
  //   Asserted: When disk spinning at full speed
  //   Held low when disk is stopped or changing direction
endmodule
