// Logisim project version1.circ as structural Verilog: 1 circuit, main circuit main
module main (
  input  [3:0] Value,
  input  [1:0] FN,
  input  GO
);

  wire and_1_out, clock_1_out, d_ff_1_qn;

  Clock clock_1 (.out(clock_1_out));
  D_Flip_Flop d_ff_1 (.D(GO), .clk(clock_1_out), .Qn(d_ff_1_qn));  // open: Q, preset, reset
  and and_1 (and_1_out, GO, d_ff_1_qn);
  Register #(.width(4)) register_1 (.en(and_1_out), .clk(clock_1_out));  // open: D, Q, clr
endmodule
