// Logisim project Lab9.circ as structural Verilog: 1 circuit, main circuit main
module main (
  input  Func,
  output [2:0] HL,
  output [2:0] FL
);

  Clock clock_1 ();  // open: out
  Register #(.width(3)) register_1 ();  // open: D, en, clk, Q, clr
  Register #(.width(3)) register_2 ();  // open: D, en, clk, Q, clr
  Multiplexer #(.width(3)) multiplexer_1 (.in0(3'b001), .out(HL), .sel(Func));  // open: in1
  Multiplexer #(.width(3)) multiplexer_2 (.in0(3'b100), .out(FL), .sel(Func));  // open: in1
  LED led_1 (.in(HL[0]));
  LED led_2 (.in(HL[1]));
  LED led_3 (.in(HL[2]));
  LED led_4 (.in(FL[0]));
  LED led_5 (.in(FL[1]));
  LED led_6 (.in(FL[2]));
endmodule
