// Logisim project Lab_11.circ as structural Verilog: 1 circuit, main circuit main
module main (
  input  [3:0] D_IN,
  input  [2:0] DA,
  input  RW,
  input  CLK,
  input  [2:0] AA,
  input  [2:0] BA,
  output [3:0] A_OUT,
  output [3:0] B_OUT
);

  Register register_1 ();  // open: D, en, clk, Q, clr
  Register register_2 ();  // open: D, en, clk, Q, clr
  Register register_3 ();  // open: D, en, clk, Q, clr
  Register register_4 ();  // open: D, en, clk, Q, clr
  Register register_5 ();  // open: D, en, clk, Q, clr
  Register register_6 ();  // open: D, en, clk, Q, clr
  Register register_7 ();  // open: D, en, clk, Q, clr
  Register register_8 ();  // open: D, en, clk, Q, clr
endmodule
